# Fritzing sketch control de aceso (saved by Fritzing 0.9.3b)
breadboards: 1

parts:
  C1 = Electrolytic Capacitor [capacitance=1µF package="100 mil [THT, electrolytic]"]
  Componente1 = Arduino Uno (Rev3)
  LCD1 = LCD screen
  LCM1602_IIC1 = LCM1602 IIC [part_number="LCM1602 IIC" chip_label="LCM1602 IIC" package="DIP (Dual Inline) [THT]"]
  Componente2 = RFID-RC522-v2
  LED1 = RGB LED - (4 legs) [package="5 mm [THT]"]
  U1 = 2-Channel 5v Relay Shield [package=relay-2ch5v10a]
  R1 = Resistor [tolerance=±5% resistance=220 package=THT]
  R2 = Resistor [tolerance=±5% resistance=220 package=THT]
  J1 = Piezo Speaker

nets:
  GND: C1.-, Componente1.GND, LCM1602_IIC1.GND, Componente2.GND, LED1.green_cathode, U1.GND, J1.pin1
  VCC: C1.+, Componente1.5V, LCM1602_IIC1.VCC, U1.VCC
  N1: Componente1.A4/SDA, LCM1602_IIC1.SDA
  N2: Componente1.A5/SCL, LCM1602_IIC1.SCL
  N3: Componente1.D9_PWM, Componente2.RST
  N4: Componente1.D10_PWM/SS, Componente2.SDA
  N5: Componente1.D11_PWM/MOSI, Componente2.MOSI
  N6: Componente1.D12/MISO, Componente2.MISO
  N7: Componente1.D13/SCK, Componente2.SCK
  N8: Componente1.D2, J1.pin2
  N9: Componente1.D5_PWM, U1.IN2
  N10: Componente1.D6_PWM, R1.Pin_0
  N11: Componente1.D7, R2.Pin_0
  3V3: Componente1.3V3, Componente2.3.3V
  VSS: LCD1.VSS, LCM1602_IIC1.VSS
  VDD: LCD1.VDD, LCM1602_IIC1.VDD
  N12: LCD1.V0, LCM1602_IIC1.V0
  N13: LCD1.RS, LCM1602_IIC1.RS
  N14: LCD1.R/W, LCM1602_IIC1.RW
  N15: LCD1.E, LCM1602_IIC1.E
  N16: LCD1.DB0, LCM1602_IIC1.D0
  N17: LCD1.DB1, LCM1602_IIC1.D1
  N18: LCD1.DB2, LCM1602_IIC1.D2
  N19: LCD1.DB3, LCM1602_IIC1.D3
  N20: LCD1.DB4, LCM1602_IIC1.D4
  N21: LCD1.DB5, LCM1602_IIC1.D5
  N22: LCD1.DB6, LCM1602_IIC1.D6
  N23: LCD1.DB7, LCM1602_IIC1.D7
  N24: LCD1.LED+, LCM1602_IIC1.A
  N25: LCD1.LED-, LCM1602_IIC1.K
  N26: LCM1602_IIC1.LED_A, LCM1602_IIC1.LED_B
  N27: LED1.common_anode, R2.Pin_1
  N28: LED1.blue_cathode, R1.Pin_1

custom parts:
  LCM1602 IIC: I2C-Module to use a 1602 or 2004 LCD on with the wire.h libory Serial LCD Modul
  RFID-RC522-v2: A simple China made RFID-RC522 Reader; do check the pin labels, as this is a MFRC522 based clone.
  2-Channel 5v Relay Shield: 2 Channel 5v Relay Shield w. 2x SPD-06VDC-SD-C
