# Fritzing sketch Untitled Sketch (saved by Fritzing 0.9.3b)
breadboards: 1

parts:
  U1 = NodeMCU V1.0
  Componente1 = RFID-RC522-v2
  LED1 = RGB LED (com. anode, rbg) [package="5 mm [THT]"]
  R1 = Resistor [tolerance=±5% resistance=220 package=THT]
  LCD1 = LCD screen
  U2 = 2-Channel 5v Relay Shield [package=relay-2ch5v10a]
  LCM1602_IIC1 = LCM1602 IIC [part_number="LCM1602 IIC" chip_label="LCM1602 IIC" package="DIP (Dual Inline) [THT]"]
  U3 = NodeMCU V1.0
  Componente2 = RFID-RC522-v2
  LED2 = RGB LED (com. anode, rbg) [package="5 mm [THT]"]
  R2 = Resistor [tolerance=±5% resistance=220 package=THT]
  R3 = Resistor [tolerance=±5% resistance=220 package=THT]
  R4 = Resistor [tolerance=±5% resistance=220 package=THT]

nets:
  N1: U1.D0, U2.IN2
  N2: U1.D1, LCM1602_IIC1.SCL
  N3: U1.D2, LCM1602_IIC1.SDA
  N4: U1.D3, Componente1.RST
  N5: U1.D4, Componente1.SDA
  VCC: U1.3V3, Componente1.3.3V, U2.VCC, LCM1602_IIC1.VCC
  GND: U1.GND, Componente1.GND, LED1.blue_cathode, U2.GND, LCM1602_IIC1.GND
  N6: U1.D5, Componente1.SCK
  N7: U1.D6, Componente1.MISO
  N8: U1.D7, Componente1.MOSI
  N9: U1.RX, R1.Pin_0
  N10: U1.A0, U3.D8
  N11: LED1.common_anode, R1.Pin_1
  VSS: LCD1.VSS, LCM1602_IIC1.VSS
  VDD: LCD1.VDD, LCM1602_IIC1.VDD
  N12: LCD1.V0, LCM1602_IIC1.V0
  N13: LCD1.RS, LCM1602_IIC1.RS
  N14: LCD1.R/W, LCM1602_IIC1.RW
  N15: LCD1.E, LCM1602_IIC1.E
  N16: LCD1.DB0, LCM1602_IIC1.D0
  N17: LCD1.DB1, LCM1602_IIC1.D1
  N18: LCD1.DB2, LCM1602_IIC1.D2
  N19: LCD1.DB3, LCM1602_IIC1.D3
  N20: LCD1.DB4, LCM1602_IIC1.D4
  N21: LCD1.DB5, LCM1602_IIC1.D5
  N22: LCD1.DB6, LCM1602_IIC1.D6
  N23: LCD1.DB7, LCM1602_IIC1.D7
  N24: LCD1.LED+, LCM1602_IIC1.A
  N25: LCD1.LED-, LCM1602_IIC1.K
  N26: LCM1602_IIC1.LED_A, LCM1602_IIC1.LED_B
  N27: U3.D3, Componente2.RST
  N28: U3.D4, Componente2.SDA
  GND_2: U3.GND, Componente2.GND, LED2.common_anode
  N29: U3.D5, Componente2.SCK
  N30: U3.D6, Componente2.MISO
  N31: U3.D7, Componente2.MOSI
  3V3: U3.3V3, Componente2.3.3V
  N32: LED2.red_cathode, R2.Pin_1
  N33: LED2.blue_cathode, R3.Pin_1
  N34: LED2.green_cathode, R4.Pin_1

custom parts:
  NodeMCU V1.0: ESP8266 based NodeMCU
  RFID-RC522-v2: A simple China made RFID-RC522 Reader; do check the pin labels, as this is a MFRC522 based clone.
  2-Channel 5v Relay Shield: 2 Channel 5v Relay Shield w. 2x SPD-06VDC-SD-C
  LCM1602 IIC: I2C-Module to use a 1602 or 2004 LCD on with the wire.h libory Serial LCD Modul
